// Logisim project 4 Bit Full Adder Circuit V2.circ as structural Verilog: 1 circuit, main circuit main
module main (
  input  A2,
  input  A1,
  input  A0,
  input  B2,
  input  B1,
  input  B0,
  output Cout,
  output Cout_2,
  output S1,
  output S0
);

  wire A1_out, A2_out, A3_out, A4_out, A5_out, O1_out, X2_out, X4_out;

  xor X1 (S0, A0, B0);
  and u_A1 (A1_out, A0, B0);
  xor X2 (X2_out, A1, A1_out);
  and u_A2 (A2_out, A1, A1_out);
  xor X3 (S1, X2_out, B1);
  and A3 (A3_out, X2_out, B1);
  or O1 (O1_out, A3_out, A2_out);
  xor X4 (X4_out, A2, O1_out);
  and A4 (A4_out, A2, O1_out);
  xor X5 (Cout_2, B2, X4_out);
  and A5 (A5_out, B2, X4_out);
  or O2 (Cout, A5_out, A4_out);

  // Notes on the sheet:
  //   S0
  //   CARRY
  //   CARRY
  //   CARRY
endmodule
