// Logisim project 4 Bit Full Adder Circuit V3.circ as structural Verilog: 1 circuit, main circuit main
module main (
  input  A3,
  input  A2,
  input  A1,
  input  A0,
  input  B3,
  input  B2,
  input  B1,
  input  B0,
  output Cout,
  output S3,
  output S2,
  output S1,
  output S0
);

  wire A1_out, A2_out, A3_out, A4_out, A5_out, A6_out, A7_out, O1_out, O2_out, X2_out, X4_out, X6_out;

  xor X1 (S0, A0, B0);
  and u_A1 (A1_out, A0, B0);
  xor X2 (X2_out, A1, A1_out);
  and u_A2 (A2_out, A1, A1_out);
  xor X3 (S1, X2_out, B1);
  and u_A3 (A3_out, X2_out, B1);
  or O1 (O1_out, A3_out, A2_out);
  xor X4 (X4_out, A2, O1_out);
  and A4 (A4_out, A2, O1_out);
  xor X5 (S2, B2, X4_out);
  and A5 (A5_out, B2, X4_out);
  or O2 (O2_out, A5_out, A4_out);
  xor X6 (X6_out, A3, O2_out);
  and A6 (A6_out, A3, O2_out);
  xor X7 (S3, B3, X6_out);
  and A7 (A7_out, B3, X6_out);
  or _03 (Cout, A7_out, A6_out);

  // Notes on the sheet:
  //   S0
  //   CARRY
  //   CARRY
  //   CARRY
endmodule
